# Fritzing sketch Untitled Sketch (saved by Fritzing 0.9.3b)
breadboards: 1

parts:
  Part1 = Arduino Uno (Rev3) - ICSP
  U1 = LCD-16X2 [package=lcd-16x2_noholes]
  R1 = Resistor [tolerance=±5% resistance=220 package=THT]
  R2 = Rotary Potentiometer (Small) [maximum_resistance=100kΩ package=THT]

nets:
  5V: Part1.5V, U1.VDD, U1.R_W, R1.Pin_0, R2.leg2
  N1: Part1.D11_PWM/MOSI, U1.E
  N2: Part1.D12/MISO, U1.RS
  GND: Part1.GND, U1.VSS, U1.K, R2.leg1
  N3: Part1.D2, U1.DB7
  N4: Part1.D3_PWM, U1.DB6
  N5: Part1.D4, U1.DB5
  N6: Part1.D5_PWM, U1.DB4
  N7: U1.VO, R2.wiper
  N8: U1.A, R1.Pin_1
